# Fritzing sketch MPU9250 (saved by Fritzing 0.9.9b)
breadboards: 1

parts:
  Part2 = Arduino Uno (Rev3) - ICSP
  Teensy1 = Teensy 4.1
  M1 = gy9250

nets:
  N1: Part2.5V, M1.pin1
  N2: Part2.GND, M1.pin2
  N3: Teensy1.GND, Teensy1.GND2#55
  N4: Teensy1.A12/D26, M1.pin3
  N5: Teensy1.A13/D27, M1.pin4
  N6: Teensy1.A14/D38, M1.pin9
  N7: Teensy1.A15/D39, M1.pin7

custom parts:
  Teensy 4.1: The Teensy is a complete USB-based microcontoller development system, in a very small footprint, capable of implementing many types of projects. All programming is done via the USB port. No special programmer is needed, only a standard micro-USB cable and a PC or Macintosh with a USB port.
  gy9250: MPU-9250 module (three-axis gyroscope + three-axis acceleration + three-axis magnetic field). The generic model from ebay et. al. rather than the Sparkfun version.
